# Fritzing sketch wiring-diagram (saved by Fritzing 0.9.6b)

parts:
  WeMos_D1_Mini1 = WeMos D1 Mini
  8_Channel_Relay1 = 8 Channel Power Relay
  J2 = Camdenboss CTB0158-9 [part_number=CTB0158-9 package=THT]
  M1 = AC-05-03
  J3 = Camdenboss CTB0158-9 [part_number=CTB0158-9 package=THT]
  J4 = Camdenboss CTB0158-9 [part_number=CTB0158-9 package=THT]
  J5 = Camdenboss CTB0158-9 [part_number=CTB0158-9 package=THT]

nets:
  3V3: WeMos_D1_Mini1.3V3, 8_Channel_Relay1.VCC
  N1: WeMos_D1_Mini1.5V, J4.terminal_2
  N2: WeMos_D1_Mini1.D0, 8_Channel_Relay1.IN8
  N3: WeMos_D1_Mini1.D1, 8_Channel_Relay1.IN1
  N4: WeMos_D1_Mini1.D2, 8_Channel_Relay1.IN2
  N5: WeMos_D1_Mini1.D3, 8_Channel_Relay1.IN3
  N6: WeMos_D1_Mini1.D4, 8_Channel_Relay1.IN4
  N7: WeMos_D1_Mini1.D5, 8_Channel_Relay1.IN5
  N8: WeMos_D1_Mini1.D6, 8_Channel_Relay1.IN6
  N9: WeMos_D1_Mini1.D7, 8_Channel_Relay1.IN7
  N10: WeMos_D1_Mini1.G, 8_Channel_Relay1.GND
  N11: 8_Channel_Relay1.COM, J5.terminal_9
  N12: J2.terminal_9, M1.pin_5
  N13: M1.pin_1, J5.terminal_1
  N14: M1.pin_2, J3.terminal_9
  N15: M1.pin_4, J4.terminal_1

notes:
  AC
  Zone1
  Zone2
  Zone3
  Zone4
  Zone5
  Zone6
  Zone7
  Zone8

custom parts:
  8 Channel Power Relay: An 8 channel power relay. The module operates at 5V.
  AC-05-03: AC-DC 220V to 5V Step-Down Power Supply Module
